# Fritzing sketch DiagramaDispensadorMedicinaCorreccion (saved by Fritzing 0.9.3b)
breadboards: 1

parts:
  Arduino_Uno = Arduino Uno (Rev3)
  Servomotor = Basic Servo
  Servomotor_2 = Basic Servo
  Servomotor_3 = Basic Servo
  Servomotor_4 = Basic Servo
  Parte4 = Max Power IR LED Kit  # not connected
  U12 = 640x480 CMOS Color Camera [package=camera_cmos_con]  # not connected
  Pi_Camera = TCM8240MD [package=tcm8240md]  # not connected
  Raspberry_Pi3 = Raspberry Pi B+
  PIR_Sensor_HC-SR501 = PIR sensor
  Buzzer = Piezo Speaker
  220Ω = Resistor [tolerance=±5% resistance=220 part_number=Resistor package=THT]
  R7 = Resistor [tolerance=±5% resistance=220 package=THT]
  R8 = Resistor [tolerance=±5% resistance=220 package=THT]
  LED = LED - 5mm [color="Red (633nm)" package="5 mm [THT]"]
  U13 = BNC [package=bnc]
  12V_battery = 4 x AAA Battery Mount  # not connected
  9v_battery = BC9VPC [package=bc9vpc]
  LCD = LCD screen
  LCD_Controller = LCM1602 IIC [part_number=" Module" chip_label="LCM1602 IIC" package="DIP (Dual Inline) [THT]"]
  Bluetooth_HC-05 = Bluetooth HC-05 Macho
  R9 = Resistor [tolerance=±5% resistance=220 package=THT]
  LED8 = smd LED [color="Yellow (585nm)" package="1206 [SMD]"]
  LED12 = smd LED [color="Green (555nm)" package="1206 [SMD]"]
  LED13 = Blue LED - 5mm

nets:
  N1: Arduino_Uno.A4/SDA, LCD_Controller.SDA
  N2: Arduino_Uno.A5/SCL, LCD_Controller.SCL
  N3: Arduino_Uno.D11_PWM/MOSI, LED12.anode
  N4: Arduino_Uno.D12/MISO, LED13.anode
  N5: Arduino_Uno.D0/RX, Bluetooth_HC-05.TXD
  N6: Arduino_Uno.D1/TX, Bluetooth_HC-05.RXD
  N7: Arduino_Uno.D2, LED.anode
  N8: Arduino_Uno.D4, LED8.anode
  N9: Arduino_Uno.D7, Buzzer.pin2
  VCC: Arduino_Uno.5V, Servomotor.vcc, Servomotor_2.vcc, Servomotor_3.vcc, Servomotor_4.vcc, LCD_Controller.VCC, Bluetooth_HC-05.VCC
  GND: Arduino_Uno.GND, Servomotor.gnd, Servomotor_2.gnd, Servomotor_3.gnd, Servomotor_4.gnd, Buzzer.pin1, 220Ω.Pin_1, R7.Pin_1, R8.Pin_1, LCD_Controller.GND, Bluetooth_HC-05.GND, R9.Pin_1
  GND_2: Raspberry_Pi3.GND, PIR_Sensor_HC-SR501.GND
  N10: Raspberry_Pi3.GPIO18, PIR_Sensor_HC-SR501.SIG
  5V: Raspberry_Pi3.5V, PIR_Sensor_HC-SR501.VDD
  N11: 220Ω.Pin_0, LED13.cathode
  N12: R7.Pin_0, LED8.cathode
  N13: R8.Pin_0, LED.cathode
  N14: U13.GND, 9v_battery.V+
  N15: U13.OUT, 9v_battery.V-
  VSS: LCD.VSS, LCD_Controller.VSS
  VDD: LCD.VDD, LCD_Controller.VDD
  N16: LCD.V0, LCD_Controller.V0
  N17: LCD.RS, LCD_Controller.RS
  N18: LCD.R/W, LCD_Controller.RW
  N19: LCD.E, LCD_Controller.E
  N20: LCD.DB0, LCD_Controller.D0
  N21: LCD.DB1, LCD_Controller.D1
  N22: LCD.DB2, LCD_Controller.D2
  N23: LCD.DB3, LCD_Controller.D3
  N24: LCD.DB4, LCD_Controller.D4
  N25: LCD.DB5, LCD_Controller.D5
  N26: LCD.DB6, LCD_Controller.D6
  N27: LCD.DB7, LCD_Controller.D7
  N28: LCD.LED+, LCD_Controller.A
  N29: LCD.LED-, LCD_Controller.K
  N30: LCD_Controller.LED_A, LCD_Controller.LED_B
  N31: R9.Pin_0, LED12.cathode

custom parts:
  LCM1602 IIC: I2C-Module to use a 1602 or 2004 LCD on with the wire.h libory Serial LCD Modul
