# Fritzing sketch DiagramaDispensadorMedicinaCorreccion1 (saved by Fritzing 0.9.3b)
breadboards: 1

parts:
  Arduino_Uno = Arduino Uno (Rev3)
  Servomotor = Basic Servo
  Servomotor_2 = Basic Servo
  Servomotor_3 = Basic Servo
  Servomotor_4 = Basic Servo
  Parte4 = Max Power IR LED Kit  # not connected
  U12 = 640x480 CMOS Color Camera [package=camera_cmos_con]  # not connected
  Pi_Camera = TCM8240MD [package=tcm8240md]  # not connected
  Raspberry_Pi3 = Raspberry Pi B+  # not connected
  Buzzer = Piezo Speaker
  220Ω = Resistor [tolerance=±5% resistance=220 part_number=Resistor package=THT]
  R7 = Resistor [tolerance=±5% resistance=220 package=THT]
  R8 = Resistor [tolerance=±5% resistance=220 package=THT]
  LED = LED - 5mm [color="Red (633nm)" package="5 mm [THT]"]
  LED5 = LED - 5mm [color="Red (633nm)" package="5 mm [THT]"]
  LED6 = LED - 5mm [color="Red (633nm)" package="5 mm [THT]"]
  U13 = BNC [package=bnc]
  12V_battery = 4 x AAA Battery Mount  # not connected
  9v_battery = BC9VPC [package=bc9vpc]
  LCD = LCD screen  # not connected
  Bluetooth_HC-05 = Bluetooth HC-05 Macho

nets:
  N1: Arduino_Uno.D12/MISO, LED6.anode
  N2: Arduino_Uno.D0/RX, Bluetooth_HC-05.TXD
  N3: Arduino_Uno.D1/TX, Bluetooth_HC-05.RXD
  N4: Arduino_Uno.D2, LED.anode
  N5: Arduino_Uno.D4, LED5.anode
  N6: Arduino_Uno.D7, Buzzer.pin2
  VCC: Arduino_Uno.5V, Servomotor.vcc, Servomotor_2.vcc, Servomotor_3.vcc, Servomotor_4.vcc, Bluetooth_HC-05.VCC
  GND: Arduino_Uno.GND, Servomotor.gnd, Servomotor_2.gnd, Servomotor_3.gnd, Servomotor_4.gnd, Buzzer.pin1, 220Ω.Pin_1, R7.Pin_1, R8.Pin_1, Bluetooth_HC-05.GND
  N7: 220Ω.Pin_0, LED6.cathode
  N8: R7.Pin_0, LED5.cathode
  N9: R8.Pin_0, LED.cathode
  N10: U13.GND, 9v_battery.V+
  N11: U13.OUT, 9v_battery.V-
