# Fritzing sketch Diagrama dispensador de medicina (saved by Fritzing 0.9.3b)
circuit board: 2.96832cm x 3.62572cm
breadboards: 1

parts:
  Componente1 = Arduino Uno (Rev3)
  R1 = Photocell (LDR) [package=THT]
  R2 = Resistor [tolerance=±5% resistance=220 package="2512 [SMD]"]
  LED1 = smd LED [color="Green (555nm)" package="0805 [SMD]"]
  J1 = Basic Servo
  J2 = Basic Servo
  LED2 = smd LED [color="Yellow (595nm)" package="0805 [SMD]"]
  R4 = Resistor [tolerance=±5% resistance=220 package="2512 [SMD]"]
  LED3 = smd LED [color="Red (660nm)" package="0805 [SMD]"]
  R5 = Resistor [tolerance=±5% resistance=220 package="2512 [SMD]"]
  R6 = Resistor [tolerance=±5% resistance=220 package="2512 [SMD]"]
  S1 = Pushbutton [package="[THT]"]
  S2 = Pushbutton [package="[THT]"]
  R7 = Resistor [tolerance=±5% resistance=220 package=THT]
  R8 = Resistor [tolerance=±5% resistance=220 package=THT]
  J3 = Basic Servo
  J4 = Basic Servo
  LCD2 = LCD screen
  Raspberry_Pi2 = Raspberry Pi 2
  U7 = BNC [package=bnc]
  U8 = LIPO-2000mAh [package=lipo-2000]
  Parte3 = Max Power IR LED Kit  # not connected
  U10 = 640x480 CMOS Color Camera [package=camera_cmos_con]  # not connected
  U11 = TCM8240MD [package=tcm8240md]
  U9 = RJ45 Jack [package=rj45-8]  # not connected
  Componente2 = Bluetooth HC-05 Macho
  U13 = BNC [package=bnc]
  U14 = LIPO-2000mAh [package=lipo-2000]

nets:
  N1: Componente1.A0, R1.pin_0, R2.Pin_1
  N2: Componente1.A2, LCD2.DB5, Raspberry_Pi2.GND
  N3: Componente1.A3, LCD2.DB6, Raspberry_Pi2.ID_SC
  N4: Componente1.A5/SCL, LCD2.DB7
  N5: Componente1.D8, J1.pulse
  N6: Componente1.D9_PWM, LCD2.E
  N7: Componente1.D10_PWM/SS, LED1.anode
  N8: Componente1.D11_PWM/MOSI, LED2.anode
  N9: Componente1.D12/MISO, J2.pulse
  N10: Componente1.D13/SCK, LED3.anode
  GND: Componente1.GND, R2.Pin_0, R4.Pin_0, R5.Pin_1, R7.Pin_0, R8.Pin_0, Raspberry_Pi2.GPIO18, Componente2.GND
  N11: Componente1.D0/RX, Componente2.TXD
  N12: Componente1.D1/TX, Componente2.RXD
  N13: Componente1.D2, S2.Pin_1, U11.DOUT5
  N14: Componente1.D3_PWM, S1.Pin_1
  N15: Componente1.D4, J4.pulse
  N16: Componente1.D5_PWM, LCD2.DB4
  N17: Componente1.D6_PWM, LCD2.RS
  N18: Componente1.D7, J3.pulse
  5V: Componente1.5V, R1.pin_1, Raspberry_Pi2.GPIO3, Componente2.VCC
  N19: LED1.cathode, R4.Pin_1
  N20: LED2.cathode, R5.Pin_0
  N21: LED3.cathode, R6.Pin_1
  N22: S1.Pin_3, S1.Pin_4, S2.Pin_3
  N23: U7.GND, U8.+
  N24: U7.OUT, U8.-
  N25: U13.GND, U14.+
  N26: U13.OUT, U14.-

notes:
  4 servos de 0-180 grados
  1 Arduino uno
  25 Cables de puente hembra-macho
  1 camara tipo TTL serial JPEG camara con NTSC video
  3 led para alertas
  6 resistencias de 220 ohmios
  2 pulsadores
  1 Pantalla Led
