# Fritzing sketch DiagramaDispensadorMedicinaCorreccion (saved by Fritzing 0.9.3b)
breadboards: 1

parts:
  Arduino_Uno = Arduino Uno (Rev3)
  Servomotor = Basic Servo
  Servomotor_2 = Basic Servo
  Servomotor_3 = Basic Servo
  Servomotor_4 = Basic Servo
  Parte4 = Max Power IR LED Kit  # not connected
  U12 = 640x480 CMOS Color Camera [package=camera_cmos_con]  # not connected
  Pi_Camare = TCM8240MD [package=tcm8240md]  # not connected
  Raspberry_Pi3 = Raspberry Pi B+
  HC-SR501_Sensor_PIR = PIR sensor
  Sound_sensor_KY-038 = Piezo Speaker
  R6 = Resistor [tolerance=±5% resistance=220 package=THT]
  R7 = Resistor [tolerance=±5% resistance=220 package=THT]
  R8 = Resistor [tolerance=±5% resistance=220 package=THT]
  LED = LED - 5mm [color="Red (633nm)" package="5 mm [THT]"]
  LED5 = LED - 5mm [color="Red (633nm)" package="5 mm [THT]"]
  LED6 = LED - 5mm [color="Red (633nm)" package="5 mm [THT]"]
  U13 = BNC [package=bnc]
  12V_battery = 4 x AAA Battery Mount  # not connected
  9v_battery = BC9VPC [package=bc9vpc]
  LCD = LCD screen
  part = LCM1602 IIC [part_number="LCM1602 IIC" chip_label="LCM1602 IIC" package="DIP (Dual Inline) [THT]"]

nets:
  N1: Arduino_Uno.A4/SDA, part.SDA
  N2: Arduino_Uno.A5/SCL, part.SCL
  N3: Arduino_Uno.D12/MISO, LED6.anode
  N4: Arduino_Uno.D2, LED.anode
  N5: Arduino_Uno.D4, LED5.anode
  N6: Arduino_Uno.D7, Sound_sensor_KY-038.pin2
  VCC: Arduino_Uno.5V, Servomotor.vcc, Servomotor_2.vcc, Servomotor_3.vcc, Servomotor_4.vcc, part.VCC
  GND: Arduino_Uno.GND, Servomotor.gnd, Servomotor_2.gnd, Servomotor_3.gnd, Servomotor_4.gnd, Sound_sensor_KY-038.pin1, R6.Pin_1, R7.Pin_1, R8.Pin_1, part.GND
  GND_2: Raspberry_Pi3.GND, HC-SR501_Sensor_PIR.GND
  N7: Raspberry_Pi3.GPIO18, HC-SR501_Sensor_PIR.SIG
  5V: Raspberry_Pi3.5V, HC-SR501_Sensor_PIR.VDD
  N8: R6.Pin_0, LED6.cathode
  N9: R7.Pin_0, LED5.cathode
  N10: R8.Pin_0, LED.cathode
  N11: U13.GND, 9v_battery.V+
  N12: U13.OUT, 9v_battery.V-
  VSS: LCD.VSS, part.VSS
  VDD: LCD.VDD, part.VDD
  N13: LCD.V0, part.V0
  N14: LCD.RS, part.RS
  N15: LCD.R/W, part.RW
  N16: LCD.E, part.E
  N17: LCD.DB0, part.D0
  N18: LCD.DB1, part.D1
  N19: LCD.DB2, part.D2
  N20: LCD.DB3, part.D3
  N21: LCD.DB4, part.D4
  N22: LCD.DB6, part.D6
  N23: LCD.DB7, part.D7
  N24: LCD.LED+, part.A
  N25: LCD.LED-, part.K
  N26: part.LED_A, part.LED_B

custom parts:
  LCM1602 IIC: I2C-Module to use a 1602 or 2004 LCD on with the wire.h libory Serial LCD Modul
